// Logisim project adder.circ as structural Verilog: 1 circuit, main circuit main
module main (
  input  [15:0] A,
  input  [15:0] B,
  input  sub,
  output [15:0] result,
  output ovf
);

  wire _0A, _1A, _2A, _3A, _4A, _5A, _6A, _7A, _8A, _9A, _10A, _11A, _12A, _13A, _14A, _15A, adder_1_cout,
       adder_2_cout, adder_3_cout, adder_4_cout, adder_5_cout, adder_6_cout, adder_7_cout, adder_8_cout,
       adder_9_cout, adder_10_cout, adder_11_cout, adder_12_cout, adder_13_cout, adder_14_cout,
       adder_15_cout, adder_16_cout, or_1_out;

  or or_1 (or_1_out, sub, 1'b0);
  Adder #(.width(1)) adder_1 (.a(A[0]), .b(_0A), .out(result[0]), .cin(or_1_out), .cout(adder_1_cout));
  Adder #(.width(1)) adder_2 (.a(A[1]), .b(_1A), .out(result[1]), .cin(adder_1_cout), .cout(adder_2_cout));
  Adder #(.width(1)) adder_3 (.a(A[2]), .b(_2A), .out(result[2]), .cin(adder_2_cout), .cout(adder_3_cout));
  Adder #(.width(1)) adder_4 (.a(A[3]), .b(_3A), .out(result[3]), .cin(adder_3_cout), .cout(adder_4_cout));
  Adder #(.width(1)) adder_5 (.a(A[4]), .b(_4A), .out(result[4]), .cin(adder_4_cout), .cout(adder_5_cout));
  Adder #(.width(1)) adder_6 (.a(A[5]), .b(_5A), .out(result[5]), .cin(adder_5_cout), .cout(adder_6_cout));
  Adder #(.width(1)) adder_7 (.a(A[6]), .b(_6A), .out(result[6]), .cin(adder_6_cout), .cout(adder_7_cout));
  Adder #(.width(1)) adder_8 (.a(A[7]), .b(_7A), .out(result[7]), .cin(adder_7_cout), .cout(adder_8_cout));
  Adder #(.width(1)) adder_9 (.a(A[8]), .b(_8A), .out(result[8]), .cin(adder_8_cout), .cout(adder_9_cout));
  Adder #(.width(1)) adder_10 (.a(A[9]), .b(_9A), .out(result[9]), .cin(adder_9_cout), .cout(adder_10_cout));
  Adder #(.width(1)) adder_11 (.a(A[10]), .b(_10A), .out(result[10]), .cin(adder_10_cout), .cout(adder_11_cout));
  Adder #(.width(1)) adder_12 (.a(A[11]), .b(_11A), .out(result[11]), .cin(adder_11_cout), .cout(adder_12_cout));
  Adder #(.width(1)) adder_13 (.a(A[12]), .b(_12A), .out(result[12]), .cin(adder_12_cout), .cout(adder_13_cout));
  Adder #(.width(1)) adder_14 (.a(A[13]), .b(_13A), .out(result[13]), .cin(adder_13_cout), .cout(adder_14_cout));
  Adder #(.width(1)) adder_15 (.a(A[14]), .b(_14A), .out(result[14]), .cin(adder_14_cout), .cout(adder_15_cout));
  Adder #(.width(1)) adder_16 (.a(A[15]), .b(_15A), .out(result[15]), .cin(adder_15_cout), .cout(adder_16_cout));
  xor xor_1 (ovf, adder_16_cout, sub);
  xor xor_2 (_0A, B[0], sub);
  xor xor_3 (_1A, B[1], sub);
  xor xor_4 (_2A, B[2], sub);
  xor xor_5 (_3A, B[3], sub);
  xor xor_6 (_4A, B[4], sub);
  xor xor_7 (_5A, B[5], sub);
  xor xor_8 (_6A, B[6], sub);
  xor xor_9 (_7A, B[7], sub);
  xor xor_10 (_8A, B[8], sub);
  xor xor_11 (_9A, B[9], sub);
  xor xor_12 (_10A, B[10], sub);
  xor xor_13 (_11A, B[11], sub);
  xor xor_14 (_12A, B[12], sub);
  xor xor_15 (_13A, B[13], sub);
  xor xor_16 (_14A, B[14], sub);
  xor xor_17 (_15A, B[15], sub);

  // Other names for the same wires on the sheet: _0 = B[0]; _1 = B[1]; _2 = B[2]; _3 = B[3]; _4 = B[4]; _5 = B[5];
  //   _6 = B[6]; _7 = B[7]; _8 = B[8]; _9 = B[9]; _10 = B[10]; _11 = B[11]; _12 = B[12]; _13 = B[13]; _14 = B[14];
  //   _15 = B[15]
endmodule
