// Logisim project circuit1a.circ as structural Verilog: 1 circuit, main circuit main
module main (
  input  A,
  input  B,
  input  C,
  output out
);

  wire and_1_out, and_2_out, or_1_out, or_2_out, or_3_out;

  or or_1 (or_1_out, A, B);
  or or_2 (or_2_out, B, C);
  and and_1 (and_1_out, A, B);
  and and_2 (and_2_out, or_1_out, or_2_out);
  or or_3 (or_3_out, and_1_out, C);
  and and_3 (out, or_3_out, and_2_out);
endmodule
