// Logisim project fsm.circ as structural Verilog: 1 circuit, main circuit main
module main (
  input  in1,
  input  in2,
  output out
);

  wire and_1_out, and_2_out, and_3_out, and_4_out, and_5_out, and_6_out, clock_1_out, D0, D1, not_1_out,
       not_2_out, not_3_out, not_4_out, not_5_out, not_6_out, nQ0, nQ1, Q0, Q1;

  not not_1 (not_1_out, in2);
  not not_2 (not_2_out, in2);
  Clock clock_1 (.out(clock_1_out));
  and and_1 (and_1_out, nQ1, in1, not_1_out);
  and and_2 (and_2_out, Q0, in1, not_2_out);
  D_Flip_Flop u_D0 (.clk(clock_1_out), .D(D0), .Q(Q0), .Qn(nQ0));  // open: preset, en, reset
  D_Flip_Flop u_D1 (.clk(clock_1_out), .D(D1), .Q(Q1), .Qn(nQ1));  // open: preset, en, reset
  not not_3 (not_3_out, in2);
  not not_4 (not_4_out, in1);
  and and_3 (and_3_out, in1, not_3_out, Q0);
  and and_4 (and_4_out, not_4_out, Q0, in2);
  not not_5 (not_5_out, in1);
  not not_6 (not_6_out, in1);
  and and_5 (and_5_out, nQ1, not_5_out, in2);
  and and_6 (and_6_out, Q0, not_6_out, in2);
  and and_7 (out, Q1, Q0);
  or or_1 (D1, and_3_out, and_4_out);
  or or_2 (D0, and_5_out, and_1_out, and_2_out, and_6_out);

  // Other names for the same wires on the sheet: _1 = in1; _2 = in2
endmodule
