// Logisim project hw4.circ as structural Verilog: 13 circuits, main circuit ProcessorMain
module ProcessorMain (
  input  reset
);

  wire ADDI, alu_2_blt__bne, ALUinB, ALUOp1, ALUOp2, ALUOp3, and_1_out, and_2_out, and_3_out, avail, BR, C,
       controlled_buffer_1_out, controlled_buffer_2_out, DMWe, in, JALf, JP, JRf, not_1_out, not_2_out,
       not_4_out, out, PosNegMux, Rdst, RWd, RWe;
  wire [2:0] ALUOp, BranchALUOp, multiplexer_3_out, Rd, Rs, Rt, Shamt, Write;
  wire [5:0] Immed;
  wire [6:0] keyb, RegisterFile_outputfromread1;
  wire [7:0] finalinput;
  wire [8:0] RegisterFile_outputfromread1_2;
  wire [11:0] Addr;
  wire [15:0] alu_1_output, ALU_for_Branch_output, ALUout, multiplexer_5_out, multiplexer_6_out,
       multiplexer_7_out, multiplexer_9_out, multiplexer_10_out, multiplexer_11_out, multiplexer_12_out,
       multiplexer_13_out, pc_1_out_5, ram_1_data, RegisterFile_outputfromread2, rom_1_data,
       signextender6to16_1_output, signextender12to16_1_output, signextendneg_1_output;

  Clock Clock (.out(C));
  PC pc_1 (.Clock(C), .Reset(reset), .Input(multiplexer_12_out), .Enable(1'b1), .out_5(pc_1_out_5));
  // Probe on rom_1_data
  DecodeInstr decodeinstr_1 (
    .InstructionInput(rom_1_data), .BR(BR), .JP(JP), .DMWe(DMWe), .RWe(RWe), .RWd(RWd), .Rdst(Rdst),
    .ALUinB(ALUinB), .ALUOp1(ALUOp1), .Addr(Addr), .Immed(Immed), .ALUOp2(ALUOp2), .Shamt(Shamt), .Rd(Rd),
    .Rt(Rt), .ALUOp3(ALUOp3), .Rs(Rs), .out(out), .in(in), .JRf(JRf), .JALf(JALf), .addiF(ADDI));
  ROM #(.addrWidth(16), .dataWidth(16)) rom_1 (.addr(pc_1_out_5), .data(rom_1_data));  // open: sel
  // Probe on Addr
  // Probe on Immed
  // Probe on Shamt
  // Probe on Rs
  // Probe on Rt
  // Probe on Rd
  Multiplexer #(.width(3), .enable("false")) multiplexer_1 (
    .in0(3'b000), .in1(3'b001), .out(BranchALUOp), .sel(and_1_out));
  and and_1 (and_1_out, Immed[5], BR);
  // Probe on {RegisterFile_outputfromread1_2, RegisterFile_outputfromread1}
  // Probe on pc_1_out_5
  Multiplexer #(.width(3), .enable("false")) multiplexer_2 (
    .in0({ALUOp1, ALUOp2, ALUOp3}), .in1(3'b001), .out(ALUOp), .sel(and_2_out));
  and and_2 (and_2_out, Immed[5], ADDI);
  not not_1 (not_1_out, C);
  // Probe on Rt
  // Probe on Rd
  ALU alu_1 (.ALUOp(3'b000), .Input1(pc_1_out_5), .Input2(16'h1), .Output(alu_1_output));  // open: ShiftAmt, blt__bne
  SignExtendNeg signextendneg_1 (.Input(Immed), .Output(signextendneg_1_output));
  // Probe on multiplexer_7_out
  Multiplexer #(.width(3), .enable("false")) multiplexer_3 (.in0(Rt), .in1(Rd), .out(multiplexer_3_out), .sel(Rdst));
  Keyboard keyboard_1 (.clk(controlled_buffer_1_out), .re(1'b1), .clr(reset), .avail(avail), .data(keyb));
  assign controlled_buffer_1_out = in ? C : 1'bz;  // Controlled_Buffer controlled_buffer_1
  // Probe on RegisterFile_outputfromread1
  or or_1 (PosNegMux, ADDI, BR);
  // Probe on alu_1_output
  // Probe on Immed
  // Probe on Immed
  // Probe on signextendneg_1_output
  // Probe on multiplexer_5_out
  RegisterFile RegisterFile (
    .Clock(not_1_out), .Reset(reset), .Enable(RWe), .WriteData(multiplexer_7_out), .WriteToWhere(Write),
    .ReadfromWhere1(Rs), .ReadfromWhere2(Rt),
    .OutputfromRead1({RegisterFile_outputfromread1_2, RegisterFile_outputfromread1}),
    .OutputfromRead2(RegisterFile_outputfromread2));
  Multiplexer #(.width(3), .enable("false")) multiplexer_4 (
    .in0(multiplexer_3_out), .in1(3'b111), .out(Write), .sel(JALf));
  TTY #(.rows(13), .cols(80), .trigger("falling")) tty_1 (
    .data(RegisterFile_outputfromread1), .clk(controlled_buffer_2_out), .clr(reset));  // open: we
  assign controlled_buffer_2_out = out ? C : 1'bz;  // Controlled_Buffer controlled_buffer_2
  SignExtender6to16 signextender6to16_1 (.Input(Immed), .Output(signextender6to16_1_output));
  Multiplexer #(.width(16), .enable("false")) multiplexer_5 (
    .in0(signextender6to16_1_output), .in1(signextendneg_1_output), .out(multiplexer_5_out), .sel(PosNegMux));
  // Probe on {RegisterFile_outputfromread1_2, RegisterFile_outputfromread1}
  // Probe on multiplexer_6_out
  Multiplexer #(.width(16), .enable("false")) multiplexer_6 (
    .in0(RegisterFile_outputfromread2), .in1(multiplexer_5_out), .out(multiplexer_6_out), .sel(ALUinB));
  // Probe on RegisterFile_outputfromread2
  // Probe on Write
  // Probe on multiplexer_12_out
  SignExtender12to16 signextender12to16_1 (.Input(Addr), .Output(signextender12to16_1_output));
  // Probe on ALU_for_Branch_output
  ALU ALU_for_Branch (
    .ALUOp(BranchALUOp), .Input1(alu_1_output), .Input2(multiplexer_5_out), .Output(ALU_for_Branch_output));  // open: ShiftAmt, blt__bne
  Multiplexer #(.width(16), .enable("false")) multiplexer_7 (
    .in0(multiplexer_9_out), .in1(alu_1_output), .out(multiplexer_7_out), .sel(JALf));
  ALU alu_2 (
    .ALUOp(ALUOp), .ShiftAmt(Shamt), .Input1({RegisterFile_outputfromread1_2, RegisterFile_outputfromread1}),
    .Input2(multiplexer_6_out), .Output(ALUout), .blt__bne(alu_2_blt__bne));
  Multiplexer #(.width(7), .enable("false")) multiplexer_8 (
    .in0(keyb), .in1({7{1'b0}}), .out(finalinput[6:0]), .sel(not_2_out));
  not not_2 (not_2_out, avail);
  // Probe on finalinput[6:0]
  not not_3 (finalinput[7], avail);
  // Probe on signextender12to16_1_output
  // Probe on nothing
  and and_3 (and_3_out, BR, alu_2_blt__bne);
  Multiplexer #(.width(16), .enable("false")) multiplexer_9 (
    .in0(multiplexer_13_out), .in1({{8{1'b0}}, finalinput}), .out(multiplexer_9_out), .sel(in));
  not not_4 (not_4_out, C);
  Multiplexer #(.width(16), .enable("false")) multiplexer_10 (
    .in0(alu_1_output), .in1(ALU_for_Branch_output), .out(multiplexer_10_out), .sel(and_3_out));
  RAM #(.addrWidth(16), .dataWidth(16), .bus("separate")) ram_1 (
    .addr(ALUout), .din(RegisterFile_outputfromread2), .data(ram_1_data), .str(DMWe), .clk(not_4_out));  // open: sel, ld, clr
  Multiplexer #(.width(16), .enable("false")) multiplexer_11 (
    .in0(multiplexer_10_out), .in1(signextender12to16_1_output), .out(multiplexer_11_out), .sel(JP));
  Multiplexer #(.width(16), .enable("false")) multiplexer_12 (
    .in0(multiplexer_11_out), .in1({RegisterFile_outputfromread1_2, RegisterFile_outputfromread1}),
    .out(multiplexer_12_out), .sel(JRf));
  Multiplexer #(.width(16), .enable("false")) multiplexer_13 (
    .in0(ALUout), .in1(ram_1_data), .out(multiplexer_13_out), .sel(RWd));

  // Other names for the same wires on the sheet: keybfinal[6:0] = finalinput[6:0]; R = reset

  // Notes on the sheet:
  //   Instrn Memory
  //   contents of rom_1 (hex, n*v repeats v):
  //   1100 1903 e040 12a0 f400 193f 983b 91ff 1fc1 91ff
  //   Data Memory
endmodule

module RegisterFile (
  input  Clock,
  input  Reset,
  input  Enable,
  input  [15:0] WriteData,
  input  [2:0] WriteToWhere,
  input  [2:0] ReadfromWhere1,
  input  [2:0] ReadfromWhere2,
  output [15:0] OutputfromRead1,
  output [15:0] OutputfromRead2
);

  wire _1in1, _1in2, _1in3, _1in4, _1in5, _1in6, _1in7, _1in8, _1in9, _1in10, _1in11, _1in12, _1in13, _1in14,
       _1in15, _1in16, _1out1, _1out2, _1out3, _1out4, _1out5, _1out6, _1out7, _1out8, _1out9, _1out10,
       _1out11, _1out12, _1out13, _1out14, _1out15, _1out16, _2ctrl0, _2ctrl1, _2ctrl2, _2ctrl3, _2ctrl4,
       _2ctrl5, _2ctrl6, _2ctrl7, _2in1, _2in2, _2in3, _2in4, _2in5, _2in6, _2in7, _2in8, _2in9, _2in10,
       _2in11, _2in12, _2in13, _2in14, _2in15, _2in16, _2out1, _2out2, _2out3, _2out4, _2out5, _2out6,
       _2out7, _2out8, _2out9, _2out10, _2out11, _2out12, _2out13, _2out14, _2out15, _2out16, _3in1, _3in2,
       _3in3, _3in4, _3in5, _3in6, _3in7, _3in8, _3in9, _3in10, _3in11, _3in12, _3in13, _3in14, _3in15,
       _3in16, _3out1, _3out2, _3out3, _3out4, _3out5, _3out6, _3out7, _3out8, _3out9, _3out10, _3out11,
       _3out12, _3out13, _3out14, _3out15, _3out16, _4in1, _4in2, _4in3, _4in4, _4in5, _4in6, _4in7, _4in8,
       _4in9, _4in10, _4in11, _4in12, _4in13, _4in14, _4in15, _4in16, _4out1, _4out2, _4out3, _4out4, _4out5,
       _4out6, _4out7, _4out8, _4out9, _4out10, _4out11, _4out12, _4out13, _4out14, _4out15, _4out16, _5in1,
       _5in2, _5in3, _5in4, _5in5, _5in6, _5in7, _5in8, _5in9, _5in10, _5in11, _5in12, _5in13, _5in14,
       _5in15, _5in16, _5out1, _5out2, _5out3, _5out4, _5out5, _5out6, _5out7, _5out8, _5out9, _5out10,
       _5out11, _5out12, _5out13, _5out14, _5out15, _5out16, _6in1, _6in2, _6in3, _6in4, _6in5, _6in6, _6in7,
       _6in8, _6in9, _6in10, _6in11, _6in12, _6in13, _6in14, _6in15, _6in16, _6out1, _6out2, _6out3, _6out4,
       _6out5, _6out6, _6out7, _6out8, _6out9, _6out10, _6out11, _6out12, _6out13, _6out14, _6out15, _6out16,
       _7in1, _7in2, _7in3, _7in4, _7in5, _7in6, _7in7, _7in8, _7in9, _7in10, _7in11, _7in12, _7in13, _7in14,
       _7in15, _7in16, _7out1, _7out2, _7out3, _7out4, _7out5, _7out6, _7out7, _7out8, _7out9, _7out10,
       _7out11, _7out12, _7out13, _7out14, _7out15, _7out16, ctrl0, ctrl1, ctrl2, ctrl3, ctrl4, ctrl5, ctrl6,
       ctrl7, in1, in2, in3, in4, in5, in6, in7, in8, in9, in10, in11, in12, in13, in14, in15, in16, out1,
       out2, out3, out4, out5, out6, out7, out8, out9, out10, out11, out12, out13, out14, out15, out16,
       wctrl0, wctrl1, wctrl2, wctrl3, wctrl4, wctrl5, wctrl6, wctrl7;
  wire [15:0] controlled_inverter_9_out, controlled_inverter_17_out, not_1_out;

  // Probe on {out16, out15, out14, out13, out12, out11, out10, out9, out8, out7, out6, out5, out4, out3, out2, out1}
  // Probe on {_1out16, _1out15, _1out14, _1out13, _1out12, _1out11, _1out10, _1out9, _1out8, _1out7, _1out6, _1out5, _1out4, _1out3, _1out2, _1out1}
  // Probe on {_2out16, _2out15, _2out14, _2out13, _2out12, _2out11, _2out10, _2out9, _2out8, _2out7, _2out6, _2out5, _2out4, _2out3, _2out2, _2out1}
  // Probe on {_3out16, _3out15, _3out14, _3out13, _3out12, _3out11, _3out10, _3out9, _3out8, _3out7, _3out6, _3out5, _3out4, _3out3, _3out2, _3out1}
  // Probe on {_4out16, _4out15, _4out14, _4out13, _4out12, _4out11, _4out10, _4out9, _4out8, _4out7, _4out6, _4out5, _4out4, _4out3, _4out2, _4out1}
  // Probe on {_5out16, _5out15, _5out14, _5out13, _5out12, _5out11, _5out10, _5out9, _5out8, _5out7, _5out6, _5out5, _5out4, _5out3, _5out2, _5out1}
  // Probe on {_6out16, _6out15, _6out14, _6out13, _6out12, _6out11, _6out10, _6out9, _6out8, _6out7, _6out6, _6out5, _6out4, _6out3, _6out2, _6out1}
  // Probe on {_7out16, _7out15, _7out14, _7out13, _7out12, _7out11, _7out10, _7out9, _7out8, _7out7, _7out6, _7out5, _7out4, _7out3, _7out2, _7out1}
  assign not_1_out = ~WriteData;  // NOT_Gate not_1, 16 bits wide
  assign {in16, in15, in14, in13, in12, in11, in10, in9, in8, in7, in6, in5, in4, in3, in2, in1} = wctrl0 ? ~not_1_out : 16'bz;  // Controlled_Inverter controlled_inverter_1
  assign {_1in16, _1in15, _1in14, _1in13, _1in12, _1in11, _1in10, _1in9, _1in8, _1in7, _1in6, _1in5, _1in4, _1in3, _1in2, _1in1} = wctrl1 ? ~not_1_out : 16'bz;  // Controlled_Inverter controlled_inverter_2
  assign {_2in16, _2in15, _2in14, _2in13, _2in12, _2in11, _2in10, _2in9, _2in8, _2in7, _2in6, _2in5, _2in4, _2in3, _2in2, _2in1} = wctrl2 ? ~not_1_out : 16'bz;  // Controlled_Inverter controlled_inverter_3
  assign {_3in16, _3in15, _3in14, _3in13, _3in12, _3in11, _3in10, _3in9, _3in8, _3in7, _3in6, _3in5, _3in4, _3in3, _3in2, _3in1} = wctrl3 ? ~not_1_out : 16'bz;  // Controlled_Inverter controlled_inverter_4
  assign {_4in16, _4in15, _4in14, _4in13, _4in12, _4in11, _4in10, _4in9, _4in8, _4in7, _4in6, _4in5, _4in4, _4in3, _4in2, _4in1} = wctrl4 ? ~not_1_out : 16'bz;  // Controlled_Inverter controlled_inverter_5
  assign {_5in16, _5in15, _5in14, _5in13, _5in12, _5in11, _5in10, _5in9, _5in8, _5in7, _5in6, _5in5, _5in4, _5in3, _5in2, _5in1} = wctrl5 ? ~not_1_out : 16'bz;  // Controlled_Inverter controlled_inverter_6
  assign {_6in16, _6in15, _6in14, _6in13, _6in12, _6in11, _6in10, _6in9, _6in8, _6in7, _6in6, _6in5, _6in4, _6in3, _6in2, _6in1} = wctrl6 ? ~not_1_out : 16'bz;  // Controlled_Inverter controlled_inverter_7
  assign {_7in16, _7in15, _7in14, _7in13, _7in12, _7in11, _7in10, _7in9, _7in8, _7in7, _7in6, _7in5, _7in4, _7in3, _7in2, _7in1} = wctrl7 ? ~not_1_out : 16'bz;  // Controlled_Inverter controlled_inverter_8
  assign controlled_inverter_9_out = ctrl0 ? ~{out16, out15, out14, out13, out12, out11, out10, out9, out8, out7, out6, out5, out4, out3, out2, out1} : 16'bz;  // Controlled_Inverter controlled_inverter_9
  assign controlled_inverter_9_out = ctrl1 ? ~{_1out16, _1out15, _1out14, _1out13, _1out12, _1out11, _1out10, _1out9, _1out8, _1out7, _1out6, _1out5, _1out4, _1out3, _1out2, _1out1} : 16'bz;  // Controlled_Inverter controlled_inverter_10
  assign controlled_inverter_9_out = ctrl2 ? ~{_2out16, _2out15, _2out14, _2out13, _2out12, _2out11, _2out10, _2out9, _2out8, _2out7, _2out6, _2out5, _2out4, _2out3, _2out2, _2out1} : 16'bz;  // Controlled_Inverter controlled_inverter_11
  assign controlled_inverter_9_out = ctrl3 ? ~{_3out16, _3out15, _3out14, _3out13, _3out12, _3out11, _3out10, _3out9, _3out8, _3out7, _3out6, _3out5, _3out4, _3out3, _3out2, _3out1} : 16'bz;  // Controlled_Inverter controlled_inverter_12
  assign controlled_inverter_9_out = ctrl4 ? ~{_4out16, _4out15, _4out14, _4out13, _4out12, _4out11, _4out10, _4out9, _4out8, _4out7, _4out6, _4out5, _4out4, _4out3, _4out2, _4out1} : 16'bz;  // Controlled_Inverter controlled_inverter_13
  assign controlled_inverter_9_out = ctrl5 ? ~{_5out16, _5out15, _5out14, _5out13, _5out12, _5out11, _5out10, _5out9, _5out8, _5out7, _5out6, _5out5, _5out4, _5out3, _5out2, _5out1} : 16'bz;  // Controlled_Inverter controlled_inverter_14
  assign controlled_inverter_9_out = ctrl6 ? ~{_6out16, _6out15, _6out14, _6out13, _6out12, _6out11, _6out10, _6out9, _6out8, _6out7, _6out6, _6out5, _6out4, _6out3, _6out2, _6out1} : 16'bz;  // Controlled_Inverter controlled_inverter_15
  assign controlled_inverter_9_out = ctrl7 ? ~{_7out16, _7out15, _7out14, _7out13, _7out12, _7out11, _7out10, _7out9, _7out8, _7out7, _7out6, _7out5, _7out4, _7out3, _7out2, _7out1} : 16'bz;  // Controlled_Inverter controlled_inverter_16
  assign controlled_inverter_17_out = _2ctrl0 ? ~{out16, out15, out14, out13, out12, out11, out10, out9, out8, out7, out6, out5, out4, out3, out2, out1} : 16'bz;  // Controlled_Inverter controlled_inverter_17
  assign controlled_inverter_17_out = _2ctrl1 ? ~{_1out16, _1out15, _1out14, _1out13, _1out12, _1out11, _1out10, _1out9, _1out8, _1out7, _1out6, _1out5, _1out4, _1out3, _1out2, _1out1} : 16'bz;  // Controlled_Inverter controlled_inverter_18
  assign controlled_inverter_17_out = _2ctrl2 ? ~{_2out16, _2out15, _2out14, _2out13, _2out12, _2out11, _2out10, _2out9, _2out8, _2out7, _2out6, _2out5, _2out4, _2out3, _2out2, _2out1} : 16'bz;  // Controlled_Inverter controlled_inverter_19
  assign controlled_inverter_17_out = _2ctrl3 ? ~{_3out16, _3out15, _3out14, _3out13, _3out12, _3out11, _3out10, _3out9, _3out8, _3out7, _3out6, _3out5, _3out4, _3out3, _3out2, _3out1} : 16'bz;  // Controlled_Inverter controlled_inverter_20
  assign controlled_inverter_17_out = _2ctrl4 ? ~{_4out16, _4out15, _4out14, _4out13, _4out12, _4out11, _4out10, _4out9, _4out8, _4out7, _4out6, _4out5, _4out4, _4out3, _4out2, _4out1} : 16'bz;  // Controlled_Inverter controlled_inverter_21
  assign controlled_inverter_17_out = _2ctrl5 ? ~{_5out16, _5out15, _5out14, _5out13, _5out12, _5out11, _5out10, _5out9, _5out8, _5out7, _5out6, _5out5, _5out4, _5out3, _5out2, _5out1} : 16'bz;  // Controlled_Inverter controlled_inverter_22
  assign controlled_inverter_17_out = _2ctrl6 ? ~{_6out16, _6out15, _6out14, _6out13, _6out12, _6out11, _6out10, _6out9, _6out8, _6out7, _6out6, _6out5, _6out4, _6out3, _6out2, _6out1} : 16'bz;  // Controlled_Inverter controlled_inverter_23
  assign controlled_inverter_17_out = _2ctrl7 ? ~{_7out16, _7out15, _7out14, _7out13, _7out12, _7out11, _7out10, _7out9, _7out8, _7out7, _7out6, _7out5, _7out4, _7out3, _7out2, _7out1} : 16'bz;  // Controlled_Inverter controlled_inverter_24
  assign OutputfromRead1 = ~controlled_inverter_9_out;  // NOT_Gate not_2, 16 bits wide
  Decoder #(.select(3)) decoder_1 (
    .out0(ctrl0), .out1(ctrl1), .out2(ctrl2), .out3(ctrl3), .out4(ctrl4), .out5(ctrl5), .out6(ctrl6),
    .out7(ctrl7), .sel(ReadfromWhere1));  // open: en
  Decoder #(.select(3)) decoder_2 (
    .out0(_2ctrl0), .out1(_2ctrl1), .out2(_2ctrl2), .out3(_2ctrl3), .out4(_2ctrl4), .out5(_2ctrl5),
    .out6(_2ctrl6), .out7(_2ctrl7), .sel(ReadfromWhere2));  // open: en
  Decoder #(.select(3)) decoder_3 (
    .out0(wctrl0), .out1(wctrl1), .out2(wctrl2), .out3(wctrl3), .out4(wctrl4), .out5(wctrl5), .out6(wctrl6),
    .out7(wctrl7), .sel(WriteToWhere));  // open: en
  assign OutputfromRead2 = ~controlled_inverter_17_out;  // NOT_Gate not_3, 16 bits wide
  D_Flip_Flop d_ff_1 (.clk(Clock), .D(in1), .Q(out1), .en(Enable), .reset(Reset));  // open: Qn, preset
  D_Flip_Flop d_ff_2 (.clk(Clock), .D(in3), .Q(out3), .en(Enable), .reset(Reset));  // open: Qn, preset
  D_Flip_Flop d_ff_3 (.clk(Clock), .D(in5), .Q(out5), .en(Enable), .reset(Reset));  // open: Qn, preset
  D_Flip_Flop d_ff_4 (.clk(Clock), .D(in7), .Q(out7), .en(Enable), .reset(Reset));  // open: Qn, preset
  D_Flip_Flop d_ff_5 (.clk(Clock), .D(in9), .Q(out9), .en(Enable), .reset(Reset));  // open: Qn, preset
  D_Flip_Flop d_ff_6 (.clk(Clock), .D(in11), .Q(out11), .en(Enable), .reset(Reset));  // open: Qn, preset
  D_Flip_Flop d_ff_7 (.clk(Clock), .D(in13), .Q(out13), .en(Enable), .reset(Reset));  // open: Qn, preset
  D_Flip_Flop d_ff_8 (.clk(Clock), .D(in15), .Q(out15), .en(Enable), .reset(Reset));  // open: Qn, preset
  D_Flip_Flop d_ff_9 (.clk(Clock), .D(_1in1), .Q(_1out1), .en(Enable), .reset(Reset));  // open: Qn, preset
  D_Flip_Flop d_ff_10 (.clk(Clock), .D(_1in3), .Q(_1out3), .en(Enable), .reset(Reset));  // open: Qn, preset
  D_Flip_Flop d_ff_11 (.clk(Clock), .D(_1in5), .Q(_1out5), .en(Enable), .reset(Reset));  // open: Qn, preset
  D_Flip_Flop d_ff_12 (.clk(Clock), .D(_1in7), .Q(_1out7), .en(Enable), .reset(Reset));  // open: Qn, preset
  D_Flip_Flop d_ff_13 (.clk(Clock), .D(_1in9), .Q(_1out9), .en(Enable), .reset(Reset));  // open: Qn, preset
  D_Flip_Flop d_ff_14 (.clk(Clock), .D(_1in11), .Q(_1out11), .en(Enable), .reset(Reset));  // open: Qn, preset
  D_Flip_Flop d_ff_15 (.clk(Clock), .D(_1in13), .Q(_1out13), .en(Enable), .reset(Reset));  // open: Qn, preset
  D_Flip_Flop d_ff_16 (.clk(Clock), .D(_1in15), .Q(_1out15), .en(Enable), .reset(Reset));  // open: Qn, preset
  D_Flip_Flop d_ff_17 (.clk(Clock), .D(_2in1), .Q(_2out1), .en(Enable), .reset(Reset));  // open: Qn, preset
  D_Flip_Flop d_ff_18 (.clk(Clock), .D(_2in3), .Q(_2out3), .en(Enable), .reset(Reset));  // open: Qn, preset
  D_Flip_Flop d_ff_19 (.clk(Clock), .D(_2in5), .Q(_2out5), .en(Enable), .reset(Reset));  // open: Qn, preset
  D_Flip_Flop d_ff_20 (.clk(Clock), .D(_2in7), .Q(_2out7), .en(Enable), .reset(Reset));  // open: Qn, preset
  D_Flip_Flop d_ff_21 (.clk(Clock), .D(_2in9), .Q(_2out9), .en(Enable), .reset(Reset));  // open: Qn, preset
  D_Flip_Flop d_ff_22 (.clk(Clock), .D(_2in11), .Q(_2out11), .en(Enable), .reset(Reset));  // open: Qn, preset
  D_Flip_Flop d_ff_23 (.clk(Clock), .D(_2in13), .Q(_2out13), .en(Enable), .reset(Reset));  // open: Qn, preset
  D_Flip_Flop d_ff_24 (.clk(Clock), .D(_2in15), .Q(_2out15), .en(Enable), .reset(Reset));  // open: Qn, preset
  D_Flip_Flop d_ff_25 (.clk(Clock), .D(in2), .Q(out2), .en(Enable), .reset(Reset));  // open: Qn, preset
  D_Flip_Flop d_ff_26 (.clk(Clock), .D(in4), .Q(out4), .en(Enable), .reset(Reset));  // open: Qn, preset
  D_Flip_Flop d_ff_27 (.clk(Clock), .D(in6), .Q(out6), .en(Enable), .reset(Reset));  // open: Qn, preset
  D_Flip_Flop d_ff_28 (.clk(Clock), .D(in8), .Q(out8), .en(Enable), .reset(Reset));  // open: Qn, preset
  D_Flip_Flop d_ff_29 (.clk(Clock), .D(in10), .Q(out10), .en(Enable), .reset(Reset));  // open: Qn, preset
  D_Flip_Flop d_ff_30 (.clk(Clock), .D(in12), .Q(out12), .en(Enable), .reset(Reset));  // open: Qn, preset
  D_Flip_Flop d_ff_31 (.clk(Clock), .D(in14), .Q(out14), .en(Enable), .reset(Reset));  // open: Qn, preset
  D_Flip_Flop d_ff_32 (.clk(Clock), .D(in16), .Q(out16), .en(Enable), .reset(Reset));  // open: Qn, preset
  D_Flip_Flop d_ff_33 (.clk(Clock), .D(_1in2), .Q(_1out2), .en(Enable), .reset(Reset));  // open: Qn, preset
  D_Flip_Flop d_ff_34 (.clk(Clock), .D(_1in4), .Q(_1out4), .en(Enable), .reset(Reset));  // open: Qn, preset
  D_Flip_Flop d_ff_35 (.clk(Clock), .D(_1in6), .Q(_1out6), .en(Enable), .reset(Reset));  // open: Qn, preset
  D_Flip_Flop d_ff_36 (.clk(Clock), .D(_1in8), .Q(_1out8), .en(Enable), .reset(Reset));  // open: Qn, preset
  D_Flip_Flop d_ff_37 (.clk(Clock), .D(_1in10), .Q(_1out10), .en(Enable), .reset(Reset));  // open: Qn, preset
  D_Flip_Flop d_ff_38 (.clk(Clock), .D(_1in12), .Q(_1out12), .en(Enable), .reset(Reset));  // open: Qn, preset
  D_Flip_Flop d_ff_39 (.clk(Clock), .D(_1in14), .Q(_1out14), .en(Enable), .reset(Reset));  // open: Qn, preset
  D_Flip_Flop d_ff_40 (.clk(Clock), .D(_1in16), .Q(_1out16), .en(Enable), .reset(Reset));  // open: Qn, preset
  D_Flip_Flop d_ff_41 (.clk(Clock), .D(_2in2), .Q(_2out2), .en(Enable), .reset(Reset));  // open: Qn, preset
  D_Flip_Flop d_ff_42 (.clk(Clock), .D(_2in4), .Q(_2out4), .en(Enable), .reset(Reset));  // open: Qn, preset
  D_Flip_Flop d_ff_43 (.clk(Clock), .D(_2in6), .Q(_2out6), .en(Enable), .reset(Reset));  // open: Qn, preset
  D_Flip_Flop d_ff_44 (.clk(Clock), .D(_2in8), .Q(_2out8), .en(Enable), .reset(Reset));  // open: Qn, preset
  D_Flip_Flop d_ff_45 (.clk(Clock), .D(_2in10), .Q(_2out10), .en(Enable), .reset(Reset));  // open: Qn, preset
  D_Flip_Flop d_ff_46 (.clk(Clock), .D(_2in12), .Q(_2out12), .en(Enable), .reset(Reset));  // open: Qn, preset
  D_Flip_Flop d_ff_47 (.clk(Clock), .D(_2in14), .Q(_2out14), .en(Enable), .reset(Reset));  // open: Qn, preset
  D_Flip_Flop d_ff_48 (.clk(Clock), .D(_2in16), .Q(_2out16), .en(Enable), .reset(Reset));  // open: Qn, preset
  D_Flip_Flop d_ff_49 (.clk(Clock), .D(_3in1), .Q(_3out1), .en(Enable), .reset(Reset));  // open: Qn, preset
  D_Flip_Flop d_ff_50 (.clk(Clock), .D(_3in3), .Q(_3out3), .en(Enable), .reset(Reset));  // open: Qn, preset
  D_Flip_Flop d_ff_51 (.clk(Clock), .D(_3in5), .Q(_3out5), .en(Enable), .reset(Reset));  // open: Qn, preset
  D_Flip_Flop d_ff_52 (.clk(Clock), .D(_3in7), .Q(_3out7), .en(Enable), .reset(Reset));  // open: Qn, preset
  D_Flip_Flop d_ff_53 (.clk(Clock), .D(_3in9), .Q(_3out9), .en(Enable), .reset(Reset));  // open: Qn, preset
  D_Flip_Flop d_ff_54 (.clk(Clock), .D(_3in11), .Q(_3out11), .en(Enable), .reset(Reset));  // open: Qn, preset
  D_Flip_Flop d_ff_55 (.clk(Clock), .D(_3in13), .Q(_3out13), .en(Enable), .reset(Reset));  // open: Qn, preset
  D_Flip_Flop d_ff_56 (.clk(Clock), .D(_3in15), .Q(_3out15), .en(Enable), .reset(Reset));  // open: Qn, preset
  D_Flip_Flop d_ff_57 (.clk(Clock), .D(_4in1), .Q(_4out1), .en(Enable), .reset(Reset));  // open: Qn, preset
  D_Flip_Flop d_ff_58 (.clk(Clock), .D(_4in3), .Q(_4out3), .en(Enable), .reset(Reset));  // open: Qn, preset
  D_Flip_Flop d_ff_59 (.clk(Clock), .D(_4in5), .Q(_4out5), .en(Enable), .reset(Reset));  // open: Qn, preset
  D_Flip_Flop d_ff_60 (.clk(Clock), .D(_4in7), .Q(_4out7), .en(Enable), .reset(Reset));  // open: Qn, preset
  D_Flip_Flop d_ff_61 (.clk(Clock), .D(_4in9), .Q(_4out9), .en(Enable), .reset(Reset));  // open: Qn, preset
  D_Flip_Flop d_ff_62 (.clk(Clock), .D(_4in11), .Q(_4out11), .en(Enable), .reset(Reset));  // open: Qn, preset
  D_Flip_Flop d_ff_63 (.clk(Clock), .D(_4in13), .Q(_4out13), .en(Enable), .reset(Reset));  // open: Qn, preset
  D_Flip_Flop d_ff_64 (.clk(Clock), .D(_4in15), .Q(_4out15), .en(Enable), .reset(Reset));  // open: Qn, preset
  D_Flip_Flop d_ff_65 (.clk(Clock), .D(_5in1), .Q(_5out1), .en(Enable), .reset(Reset));  // open: Qn, preset
  D_Flip_Flop d_ff_66 (.clk(Clock), .D(_5in3), .Q(_5out3), .en(Enable), .reset(Reset));  // open: Qn, preset
  D_Flip_Flop d_ff_67 (.clk(Clock), .D(_5in5), .Q(_5out5), .en(Enable), .reset(Reset));  // open: Qn, preset
  D_Flip_Flop d_ff_68 (.clk(Clock), .D(_5in7), .Q(_5out7), .en(Enable), .reset(Reset));  // open: Qn, preset
  D_Flip_Flop d_ff_69 (.clk(Clock), .D(_5in9), .Q(_5out9), .en(Enable), .reset(Reset));  // open: Qn, preset
  D_Flip_Flop d_ff_70 (.clk(Clock), .D(_5in11), .Q(_5out11), .en(Enable), .reset(Reset));  // open: Qn, preset
  D_Flip_Flop d_ff_71 (.clk(Clock), .D(_5in13), .Q(_5out13), .en(Enable), .reset(Reset));  // open: Qn, preset
  D_Flip_Flop d_ff_72 (.clk(Clock), .D(_5in15), .Q(_5out15), .en(Enable), .reset(Reset));  // open: Qn, preset
  D_Flip_Flop d_ff_73 (.clk(Clock), .D(_3in2), .Q(_3out2), .en(Enable), .reset(Reset));  // open: Qn, preset
  D_Flip_Flop d_ff_74 (.clk(Clock), .D(_3in4), .Q(_3out4), .en(Enable), .reset(Reset));  // open: Qn, preset
  D_Flip_Flop d_ff_75 (.clk(Clock), .D(_3in6), .Q(_3out6), .en(Enable), .reset(Reset));  // open: Qn, preset
  D_Flip_Flop d_ff_76 (.clk(Clock), .D(_3in8), .Q(_3out8), .en(Enable), .reset(Reset));  // open: Qn, preset
  D_Flip_Flop d_ff_77 (.clk(Clock), .D(_3in10), .Q(_3out10), .en(Enable), .reset(Reset));  // open: Qn, preset
  D_Flip_Flop d_ff_78 (.clk(Clock), .D(_3in12), .Q(_3out12), .en(Enable), .reset(Reset));  // open: Qn, preset
  D_Flip_Flop d_ff_79 (.clk(Clock), .D(_3in14), .Q(_3out14), .en(Enable), .reset(Reset));  // open: Qn, preset
  D_Flip_Flop d_ff_80 (.clk(Clock), .D(_3in16), .Q(_3out16), .en(Enable), .reset(Reset));  // open: Qn, preset
  D_Flip_Flop d_ff_81 (.clk(Clock), .D(_4in2), .Q(_4out2), .en(Enable), .reset(Reset));  // open: Qn, preset
  D_Flip_Flop d_ff_82 (.clk(Clock), .D(_4in4), .Q(_4out4), .en(Enable), .reset(Reset));  // open: Qn, preset
  D_Flip_Flop d_ff_83 (.clk(Clock), .D(_4in6), .Q(_4out6), .en(Enable), .reset(Reset));  // open: Qn, preset
  D_Flip_Flop d_ff_84 (.clk(Clock), .D(_4in8), .Q(_4out8), .en(Enable), .reset(Reset));  // open: Qn, preset
  D_Flip_Flop d_ff_85 (.clk(Clock), .D(_4in10), .Q(_4out10), .en(Enable), .reset(Reset));  // open: Qn, preset
  D_Flip_Flop d_ff_86 (.clk(Clock), .D(_4in12), .Q(_4out12), .en(Enable), .reset(Reset));  // open: Qn, preset
  D_Flip_Flop d_ff_87 (.clk(Clock), .D(_4in14), .Q(_4out14), .en(Enable), .reset(Reset));  // open: Qn, preset
  D_Flip_Flop d_ff_88 (.clk(Clock), .D(_4in16), .Q(_4out16), .en(Enable), .reset(Reset));  // open: Qn, preset
  D_Flip_Flop d_ff_89 (.clk(Clock), .D(_5in2), .Q(_5out2), .en(Enable), .reset(Reset));  // open: Qn, preset
  D_Flip_Flop d_ff_90 (.clk(Clock), .D(_5in4), .Q(_5out4), .en(Enable), .reset(Reset));  // open: Qn, preset
  D_Flip_Flop d_ff_91 (.clk(Clock), .D(_5in6), .Q(_5out6), .en(Enable), .reset(Reset));  // open: Qn, preset
  D_Flip_Flop d_ff_92 (.clk(Clock), .D(_5in8), .Q(_5out8), .en(Enable), .reset(Reset));  // open: Qn, preset
  D_Flip_Flop d_ff_93 (.clk(Clock), .D(_5in10), .Q(_5out10), .en(Enable), .reset(Reset));  // open: Qn, preset
  D_Flip_Flop d_ff_94 (.clk(Clock), .D(_5in12), .Q(_5out12), .en(Enable), .reset(Reset));  // open: Qn, preset
  D_Flip_Flop d_ff_95 (.clk(Clock), .D(_5in14), .Q(_5out14), .en(Enable), .reset(Reset));  // open: Qn, preset
  D_Flip_Flop d_ff_96 (.clk(Clock), .D(_5in16), .Q(_5out16), .en(Enable), .reset(Reset));  // open: Qn, preset
  D_Flip_Flop d_ff_97 (.clk(Clock), .D(_6in1), .Q(_6out1), .en(Enable), .reset(Reset));  // open: Qn, preset
  D_Flip_Flop d_ff_98 (.clk(Clock), .D(_6in3), .Q(_6out3), .en(Enable), .reset(Reset));  // open: Qn, preset
  D_Flip_Flop d_ff_99 (.clk(Clock), .D(_6in5), .Q(_6out5), .en(Enable), .reset(Reset));  // open: Qn, preset
  D_Flip_Flop d_ff_100 (.clk(Clock), .D(_6in7), .Q(_6out7), .en(Enable), .reset(Reset));  // open: Qn, preset
  D_Flip_Flop d_ff_101 (.clk(Clock), .D(_6in9), .Q(_6out9), .en(Enable), .reset(Reset));  // open: Qn, preset
  D_Flip_Flop d_ff_102 (.clk(Clock), .D(_6in11), .Q(_6out11), .en(Enable), .reset(Reset));  // open: Qn, preset
  D_Flip_Flop d_ff_103 (.clk(Clock), .D(_6in13), .Q(_6out13), .en(Enable), .reset(Reset));  // open: Qn, preset
  D_Flip_Flop d_ff_104 (.clk(Clock), .D(_6in15), .Q(_6out15), .en(Enable), .reset(Reset));  // open: Qn, preset
  D_Flip_Flop d_ff_105 (.clk(Clock), .D(_7in1), .Q(_7out1), .en(Enable), .reset(Reset));  // open: Qn, preset
  D_Flip_Flop d_ff_106 (.clk(Clock), .D(_7in3), .Q(_7out3), .en(Enable), .reset(Reset));  // open: Qn, preset
  D_Flip_Flop d_ff_107 (.clk(Clock), .D(_7in5), .Q(_7out5), .en(Enable), .reset(Reset));  // open: Qn, preset
  D_Flip_Flop d_ff_108 (.clk(Clock), .D(_7in7), .Q(_7out7), .en(Enable), .reset(Reset));  // open: Qn, preset
  D_Flip_Flop d_ff_109 (.clk(Clock), .D(_7in9), .Q(_7out9), .en(Enable), .reset(Reset));  // open: Qn, preset
  D_Flip_Flop d_ff_110 (.clk(Clock), .D(_7in11), .Q(_7out11), .en(Enable), .reset(Reset));  // open: Qn, preset
  D_Flip_Flop d_ff_111 (.clk(Clock), .D(_7in13), .Q(_7out13), .en(Enable), .reset(Reset));  // open: Qn, preset
  D_Flip_Flop d_ff_112 (.clk(Clock), .D(_7in15), .Q(_7out15), .en(Enable), .reset(Reset));  // open: Qn, preset
  D_Flip_Flop d_ff_113 (.clk(Clock), .D(_6in2), .Q(_6out2), .en(Enable), .reset(Reset));  // open: Qn, preset
  D_Flip_Flop d_ff_114 (.clk(Clock), .D(_6in4), .Q(_6out4), .en(Enable), .reset(Reset));  // open: Qn, preset
  D_Flip_Flop d_ff_115 (.clk(Clock), .D(_6in6), .Q(_6out6), .en(Enable), .reset(Reset));  // open: Qn, preset
  D_Flip_Flop d_ff_116 (.clk(Clock), .D(_6in8), .Q(_6out8), .en(Enable), .reset(Reset));  // open: Qn, preset
  D_Flip_Flop d_ff_117 (.clk(Clock), .D(_6in10), .Q(_6out10), .en(Enable), .reset(Reset));  // open: Qn, preset
  D_Flip_Flop d_ff_118 (.clk(Clock), .D(_6in12), .Q(_6out12), .en(Enable), .reset(Reset));  // open: Qn, preset
  D_Flip_Flop d_ff_119 (.clk(Clock), .D(_6in14), .Q(_6out14), .en(Enable), .reset(Reset));  // open: Qn, preset
  D_Flip_Flop d_ff_120 (.clk(Clock), .D(in16), .Q(_6out16), .en(Enable), .reset(Reset));  // open: Qn, preset
  D_Flip_Flop d_ff_121 (.clk(Clock), .D(_7in2), .Q(_7out2), .en(Enable), .reset(Reset));  // open: Qn, preset
  D_Flip_Flop d_ff_122 (.clk(Clock), .D(_7in4), .Q(_7out4), .en(Enable), .reset(Reset));  // open: Qn, preset
  D_Flip_Flop d_ff_123 (.clk(Clock), .D(_7in6), .Q(_7out6), .en(Enable), .reset(Reset));  // open: Qn, preset
  D_Flip_Flop d_ff_124 (.clk(Clock), .D(_7in8), .Q(_7out8), .en(Enable), .reset(Reset));  // open: Qn, preset
  D_Flip_Flop d_ff_125 (.clk(Clock), .D(_7in10), .Q(_7out10), .en(Enable), .reset(Reset));  // open: Qn, preset
  D_Flip_Flop d_ff_126 (.clk(Clock), .D(_7in12), .Q(_7out12), .en(Enable), .reset(Reset));  // open: Qn, preset
  D_Flip_Flop d_ff_127 (.clk(Clock), .D(_7in14), .Q(_7out14), .en(Enable), .reset(Reset));  // open: Qn, preset
  D_Flip_Flop d_ff_128 (.clk(Clock), .D(_7in16), .Q(_7out16), .en(Enable), .reset(Reset));  // open: Qn, preset

  // Other names for the same wires on the sheet: E = Enable;
  //   InReg0[15:0] = {in16, in15, in14, in13, in12, in11, in10, in9, in8, in7, in6, in5, in4, in3, in2, in1};
  //   InReg1[15:0] = {_1in16, _1in15, _1in14, _1in13, _1in12, _1in11, _1in10, _1in9, _1in8, _1in7, _1in6, _1in5, _1in4, _1in3, _1in2, _1in1};
  //   InReg2[15:0] = {_2in16, _2in15, _2in14, _2in13, _2in12, _2in11, _2in10, _2in9, _2in8, _2in7, _2in6, _2in5, _2in4, _2in3, _2in2, _2in1};
  //   InReg3[15:0] = {_3in16, _3in15, _3in14, _3in13, _3in12, _3in11, _3in10, _3in9, _3in8, _3in7, _3in6, _3in5, _3in4, _3in3, _3in2, _3in1};
  //   InReg4[15:0] = {_4in16, _4in15, _4in14, _4in13, _4in12, _4in11, _4in10, _4in9, _4in8, _4in7, _4in6, _4in5, _4in4, _4in3, _4in2, _4in1};
  //   InReg5[15:0] = {_5in16, _5in15, _5in14, _5in13, _5in12, _5in11, _5in10, _5in9, _5in8, _5in7, _5in6, _5in5, _5in4, _5in3, _5in2, _5in1};
  //   InReg6[15:0] = {_6in16, _6in15, _6in14, _6in13, _6in12, _6in11, _6in10, _6in9, _6in8, _6in7, _6in6, _6in5, _6in4, _6in3, _6in2, _6in1};
  //   InReg7[15:0] = {_7in16, _7in15, _7in14, _7in13, _7in12, _7in11, _7in10, _7in9, _7in8, _7in7, _7in6, _7in5, _7in4, _7in3, _7in2, _7in1};
  //   OutReg0[15:0] = {out16, out15, out14, out13, out12, out11, out10, out9, out8, out7, out6, out5, out4, out3, out2, out1};
  //   OutReg1[15:0] = {_1out16, _1out15, _1out14, _1out13, _1out12, _1out11, _1out10, _1out9, _1out8, _1out7, _1out6, _1out5, _1out4, _1out3, _1out2, _1out1};
  //   OutReg2[15:0] = {_2out16, _2out15, _2out14, _2out13, _2out12, _2out11, _2out10, _2out9, _2out8, _2out7, _2out6, _2out5, _2out4, _2out3, _2out2, _2out1};
  //   OutReg3[15:0] = {_3out16, _3out15, _3out14, _3out13, _3out12, _3out11, _3out10, _3out9, _3out8, _3out7, _3out6, _3out5, _3out4, _3out3, _3out2, _3out1};
  //   OutReg4[15:0] = {_4out16, _4out15, _4out14, _4out13, _4out12, _4out11, _4out10, _4out9, _4out8, _4out7, _4out6, _4out5, _4out4, _4out3, _4out2, _4out1};
  //   OutReg5[15:0] = {_5out16, _5out15, _5out14, _5out13, _5out12, _5out11, _5out10, _5out9, _5out8, _5out7, _5out6, _5out5, _5out4, _5out3, _5out2, _5out1};
  //   OutReg6[15:0] = {_6out16, _6out15, _6out14, _6out13, _6out12, _6out11, _6out10, _6out9, _6out8, _6out7, _6out6, _6out5, _6out4, _6out3, _6out2, _6out1};
  //   OutReg7[15:0] = {_7out16, _7out15, _7out14, _7out13, _7out12, _7out11, _7out10, _7out9, _7out8, _7out7, _7out6, _7out5, _7out4, _7out3, _7out2, _7out1};
  //   R = Reset; r1[2:0] = ReadfromWhere1; r2[2:0] = ReadfromWhere2; w1[2:0] = WriteToWhere

  // Notes on the sheet:
  //   <-- Global Register Inputs
  //   Register 0
  //   Register 1
  //   Register 2
  //   Register 3
  //   Register 4
  //   Register 5
  //   Register 6
  //   Register 7
endmodule

module DecodeInstr (
  input  [15:0] InstructionInput,
  output BR,
  output JP,
  output DMWe,
  output RWe,
  output RWd,
  output Rdst,
  output ALUinB,
  output ALUOp1,
  output [11:0] Addr,
  output [5:0] Immed,
  output ALUOp2,
  output [2:0] Shamt,
  output [2:0] Rd,
  output [2:0] Rt,
  output ALUOp3,
  output [2:0] Rs,
  output out,
  output in,
  output JRf,
  output JALf,
  output addiF
);

  wire add, blt, bne, j, \not , sll, srl, sub, \xor ;

  Decoder #(.select(4), .enable("false")) decoder_1 (
    .out0(add), .out1(addiF), .out2(sub), .out3(\not ), .out4(\xor ), .out5(sll), .out6(srl), .out7(RWd),
    .out8(DMWe), .out9(bne), .out10(blt), .out11(j), .out12(JRf), .out13(JALf), .out14(in), .out15(out),
    .sel(InstructionInput[15:12]));
  or or_1 (BR, bne, blt);
  or or_2 (JP, JALf, j);
  or or_3 (RWe, RWd, \not , \xor , sll, srl, addiF, add, sub, in, JALf);
  or or_4 (Rdst, srl, sll, \xor , \not , add, sub);
  or or_5 (ALUinB, addiF, RWd, DMWe);
  or or_6 (ALUOp1, \not , sll, bne, srl);
  or or_7 (ALUOp2, bne, \xor , sll, srl);
  or or_8 (ALUOp3, blt, sub, srl);

  assign Addr = InstructionInput[11:0];
  assign Immed = InstructionInput[5:0];
  assign Rd = InstructionInput[5:3];
  assign Rs = InstructionInput[11:9];
  assign Rt = InstructionInput[8:6];
  assign Shamt = InstructionInput[2:0];

  // Other names for the same wires on the sheet: addi = addiF; Address[11:0] = InstructionInput[11:0];
  //   Immediate[5:0] = InstructionInput[5:0]; input = in; Opcode[3:0] = InstructionInput[15:12]; jal = JALf; jr = JRf;
  //   lw = RWd; output = out; sw = DMWe
endmodule

module ALU (
  input  [2:0] ALUOp,
  input  [2:0] ShiftAmt,
  input  [15:0] Input1,
  input  [15:0] Input2,
  output [15:0] Output,
  output blt__bne
);

  wire alu_slice_1_carry_out, alu_slice_2_carry_out, alu_slice_3_carry_out, alu_slice_4_carry_out,
       alu_slice_5_carry_out, alu_slice_6_carry_out, alu_slice_7_carry_out, alu_slice_8_carry_out,
       alu_slice_9_carry_out, alu_slice_10_carry_out, alu_slice_11_carry_out, alu_slice_12_carry_out,
       alu_slice_13_carry_out, alu_slice_14_carry_out, alu_slice_15_carry_out, alu_slice_16_carry_out,
       and_1_out, blt__A___B, Neq;
  wire [15:0] ALUOut, ShiftL, ShiftR;

  ALU_Slice alu_slice_1 (
    .Input_A(Input1[0]), .Input_B(Input2[0]), .Carry_In(ALUOp[0]), .Add_Subtract_Control(ALUOp[0]),
    .Carry_Out(alu_slice_1_carry_out), .Control(ALUOp[2:1]), .Output_Q(ALUOut[0]));
  ALU_Slice alu_slice_2 (
    .Input_A(Input1[1]), .Input_B(Input2[1]), .Carry_In(alu_slice_1_carry_out),
    .Add_Subtract_Control(ALUOp[0]), .Carry_Out(alu_slice_2_carry_out), .Control(ALUOp[2:1]),
    .Output_Q(ALUOut[1]));
  ALU_Slice alu_slice_3 (
    .Input_A(Input1[2]), .Input_B(Input2[2]), .Carry_In(alu_slice_2_carry_out),
    .Add_Subtract_Control(ALUOp[0]), .Carry_Out(alu_slice_3_carry_out), .Control(ALUOp[2:1]),
    .Output_Q(ALUOut[2]));
  ALU_Slice alu_slice_4 (
    .Input_A(Input1[3]), .Input_B(Input2[3]), .Carry_In(alu_slice_3_carry_out),
    .Add_Subtract_Control(ALUOp[0]), .Carry_Out(alu_slice_4_carry_out), .Control(ALUOp[2:1]),
    .Output_Q(ALUOut[3]));
  ALU_Slice alu_slice_5 (
    .Input_A(Input1[4]), .Input_B(Input2[4]), .Carry_In(alu_slice_4_carry_out),
    .Add_Subtract_Control(ALUOp[0]), .Carry_Out(alu_slice_5_carry_out), .Control(ALUOp[2:1]),
    .Output_Q(ALUOut[4]));
  ALU_Slice alu_slice_6 (
    .Input_A(Input1[5]), .Input_B(Input2[5]), .Carry_In(alu_slice_5_carry_out),
    .Add_Subtract_Control(ALUOp[0]), .Carry_Out(alu_slice_6_carry_out), .Control(ALUOp[2:1]),
    .Output_Q(ALUOut[5]));
  ALU_Slice alu_slice_7 (
    .Input_A(Input1[6]), .Input_B(Input2[6]), .Carry_In(alu_slice_6_carry_out),
    .Add_Subtract_Control(ALUOp[0]), .Carry_Out(alu_slice_7_carry_out), .Control(ALUOp[2:1]),
    .Output_Q(ALUOut[6]));
  ALU_Slice alu_slice_8 (
    .Input_A(Input1[7]), .Input_B(Input2[7]), .Carry_In(alu_slice_7_carry_out),
    .Add_Subtract_Control(ALUOp[0]), .Carry_Out(alu_slice_8_carry_out), .Control(ALUOp[2:1]),
    .Output_Q(ALUOut[7]));
  ALU_Slice alu_slice_9 (
    .Input_A(Input1[8]), .Input_B(Input2[8]), .Carry_In(alu_slice_8_carry_out),
    .Add_Subtract_Control(ALUOp[0]), .Carry_Out(alu_slice_9_carry_out), .Control(ALUOp[2:1]),
    .Output_Q(ALUOut[8]));
  ALU_Slice alu_slice_10 (
    .Input_A(Input1[9]), .Input_B(Input2[9]), .Carry_In(alu_slice_9_carry_out),
    .Add_Subtract_Control(ALUOp[0]), .Carry_Out(alu_slice_10_carry_out), .Control(ALUOp[2:1]),
    .Output_Q(ALUOut[9]));
  ALU_Slice alu_slice_11 (
    .Input_A(Input1[10]), .Input_B(Input2[10]), .Carry_In(alu_slice_10_carry_out),
    .Add_Subtract_Control(ALUOp[0]), .Carry_Out(alu_slice_11_carry_out), .Control(ALUOp[2:1]),
    .Output_Q(ALUOut[10]));
  ALU_Slice alu_slice_12 (
    .Input_A(Input1[11]), .Input_B(Input2[11]), .Carry_In(alu_slice_11_carry_out),
    .Add_Subtract_Control(ALUOp[0]), .Carry_Out(alu_slice_12_carry_out), .Control(ALUOp[2:1]),
    .Output_Q(ALUOut[11]));
  ALU_Slice alu_slice_13 (
    .Input_A(Input1[12]), .Input_B(Input2[12]), .Carry_In(alu_slice_12_carry_out),
    .Add_Subtract_Control(ALUOp[0]), .Carry_Out(alu_slice_13_carry_out), .Control(ALUOp[2:1]),
    .Output_Q(ALUOut[12]));
  ALU_Slice alu_slice_14 (
    .Input_A(Input1[13]), .Input_B(Input2[13]), .Carry_In(alu_slice_13_carry_out),
    .Add_Subtract_Control(ALUOp[0]), .Carry_Out(alu_slice_14_carry_out), .Control(ALUOp[2:1]),
    .Output_Q(ALUOut[13]));
  ALU_Slice alu_slice_15 (
    .Input_A(Input1[14]), .Input_B(Input2[14]), .Carry_In(alu_slice_14_carry_out),
    .Add_Subtract_Control(ALUOp[0]), .Carry_Out(alu_slice_15_carry_out), .Control(ALUOp[2:1]),
    .Output_Q(ALUOut[14]));
  ALU_Slice alu_slice_16 (
    .Input_A(Input1[15]), .Input_B(Input2[15]), .Carry_In(alu_slice_15_carry_out),
    .Add_Subtract_Control(ALUOp[0]), .Carry_Out(alu_slice_16_carry_out), .Control(ALUOp[2:1]),
    .Output_Q(ALUOut[15]));
  not not_1 (blt__A___B, alu_slice_16_carry_out);
  and and_1 (and_1_out, ALUOut[0], ALUOut[1], ALUOut[2], ALUOut[3], ALUOut[4], ALUOut[5], ALUOut[6], ALUOut[7], ALUOut[8], ALUOut[9], ALUOut[10], ALUOut[11], ALUOut[12], ALUOut[13], ALUOut[14], ALUOut[15]);
  not not_2 (Neq, and_1_out);
  LShift lshift_1 (
    .ShiftAmt(ShiftAmt), .in15(Input1[0]), .in14(Input1[1]), .in13(Input1[2]), .in12(Input1[3]),
    .in11(Input1[4]), .in10(Input1[5]), .in9(Input1[6]), .in8(Input1[7]), .in7(Input1[8]), .in6(Input1[9]),
    .in5(Input1[10]), .in4(Input1[11]), .in3(Input1[12]), .in2(Input1[13]), .in1(Input1[14]),
    .in0(Input1[15]), .out15(ShiftL[0]), .out14(ShiftL[1]), .out13(ShiftL[2]), .out12(ShiftL[3]),
    .out11(ShiftL[4]), .out10(ShiftL[5]), .out9(ShiftL[6]), .out8(ShiftL[7]), .out7(ShiftL[8]),
    .out6(ShiftL[9]), .out5(ShiftL[10]), .out4(ShiftL[11]), .out3(ShiftL[12]), .out2(ShiftL[13]),
    .out1(ShiftL[14]), .out0(ShiftL[15]));
  RShift rshift_1 (
    .ShiftAmt(ShiftAmt), .in15(Input1[0]), .in14(Input1[1]), .in13(Input1[2]), .in12(Input1[3]),
    .in11(Input1[4]), .in10(Input1[5]), .in9(Input1[6]), .in8(Input1[7]), .in7(Input1[8]), .in6(Input1[9]),
    .in5(Input1[10]), .in4(Input1[11]), .in3(Input1[12]), .in2(Input1[13]), .in1(Input1[14]),
    .in0(Input1[15]), .out15(ShiftR[0]), .out14(ShiftR[1]), .out13(ShiftR[2]), .out12(ShiftR[3]),
    .out11(ShiftR[4]), .out10(ShiftR[5]), .out9(ShiftR[6]), .out8(ShiftR[7]), .out7(ShiftR[8]),
    .out6(ShiftR[9]), .out5(ShiftR[10]), .out4(ShiftR[11]), .out3(ShiftR[12]), .out2(ShiftR[13]),
    .out1(ShiftR[14]), .out0(ShiftR[15]));
  Multiplexer #(.select(3), .width(16), .enable("false")) multiplexer_1 (
    .in0(ALUOut), .in1(ALUOut), .in2(ALUOut), .in3(ALUOut), .in4(ALUOut), .in6(ShiftL), .in7(ShiftR),
    .out(Output), .sel(ALUOp));  // open: in5
  Multiplexer #(.select(3), .enable("false")) multiplexer_2 (
    .in1(blt__A___B), .in6(Neq), .out(blt__bne), .sel(ALUOp));  // open: in0, in2, in3, in4, in5, in7

  // Other names for the same wires on the sheet: _3Op[2:0] = ALUOp; as = ALUOp[0]; Q0 = ALUOut[0]; Q1 = ALUOut[1];
  //   Q2 = ALUOut[2]; Q3 = ALUOut[3]; Q4 = ALUOut[4]; Q5 = ALUOut[5]; Q6 = ALUOut[6]; Q7 = ALUOut[7]; Q8 = ALUOut[8];
  //   Q9 = ALUOut[9]; Q10 = ALUOut[10]; Q11 = ALUOut[11]; Q12 = ALUOut[12]; Q13 = ALUOut[13]; Q14 = ALUOut[14];
  //   Q15 = ALUOut[15]; amt[2:0] = ShiftAmt; _0 = Input1[0]; _1 = Input1[1]; _2 = Input1[2]; _3 = Input1[3];
  //   _4 = Input1[4]; _5 = Input1[5]; _6 = Input1[6]; _7 = Input1[7]; _8 = Input1[8]; _9 = Input1[9];
  //   _10 = Input1[10]; _11 = Input1[11]; _12 = Input1[12]; _13 = Input1[13]; _14 = Input1[14]; _15 = Input1[15];
  //   B0 = Input2[0]; _1B = Input2[1]; _2B = Input2[2]; _3B = Input2[3]; _4B = Input2[4]; _5B = Input2[5];
  //   _6B = Input2[6]; _7B = Input2[7]; _8B = Input2[8]; _9B = Input2[9]; _10B = Input2[10]; _11B = Input2[11];
  //   _12B = Input2[12]; _13B = Input2[13]; _14B = Input2[14]; _15B = Input2[15]; Op[1:0] = ALUOp[2:1]

  // Notes on the sheet:
  //   Add/Sub/XOR/NOT/Equality
  //   Shift Left
  //   Shift Right
endmodule

module ALU_Slice (
  input  Carry_In,
  input  Input_A,
  input  Input_B,
  input  [1:0] Control,
  input  Add_Subtract_Control,
  output Output_Q,
  output Carry_Out
);

  wire n1_bit_adder_1_sum, not_1_out, xnor_1_out, xor_1_out, xor_2_out;

  xor xor_1 (xor_1_out, Input_A, Input_B);
  not not_1 (not_1_out, Input_A);
  xnor xnor_1 (xnor_1_out, Input_A, Input_B);
  xor xor_2 (xor_2_out, Input_B, Add_Subtract_Control);
  _1_Bit_Adder u_1_bit_adder_1 (
    .A(Input_A), .B(xor_2_out), .Carry_in(Carry_In), .Carry_Out(Carry_Out), .Sum(n1_bit_adder_1_sum));
  Multiplexer #(.select(2), .enable("false")) multiplexer_1 (
    .in0(n1_bit_adder_1_sum), .in1(xor_1_out), .in2(not_1_out), .in3(xnor_1_out), .out(Output_Q),
    .sel(Control));

  // Notes on the sheet:
  //   NOT
  //   XNOR (equality)
  //   XOR
  //   Add/Subtract
endmodule

module LShift (
  input  [2:0] ShiftAmt,
  input  in15,
  input  in14,
  input  in13,
  input  in12,
  input  in11,
  input  in10,
  input  in9,
  input  in8,
  input  in7,
  input  in6,
  input  in5,
  input  in4,
  input  in3,
  input  in2,
  input  in1,
  input  in0,
  output out15,
  output out14,
  output out13,
  output out12,
  output out11,
  output out10,
  output out9,
  output out8,
  output out7,
  output out6,
  output out5,
  output out4,
  output out3,
  output out2,
  output out1,
  output out0
);

  wire multiplexer_1_out, multiplexer_2_out, multiplexer_3_out, multiplexer_4_out, multiplexer_5_out,
       multiplexer_6_out, multiplexer_7_out, multiplexer_8_out, multiplexer_9_out, multiplexer_10_out,
       multiplexer_11_out, multiplexer_12_out, multiplexer_13_out, multiplexer_14_out, multiplexer_15_out,
       multiplexer_16_out, multiplexer_17_out, multiplexer_18_out, multiplexer_19_out, multiplexer_20_out,
       multiplexer_21_out, multiplexer_22_out, multiplexer_23_out, multiplexer_24_out, multiplexer_25_out,
       multiplexer_26_out, multiplexer_27_out, multiplexer_28_out, multiplexer_29_out, multiplexer_30_out,
       multiplexer_31_out, multiplexer_32_out;

  Multiplexer #(.enable("false")) multiplexer_1 (.in0(in15), .in1(1'b0), .out(multiplexer_1_out), .sel(ShiftAmt[0]));
  Multiplexer #(.enable("false")) multiplexer_2 (.in0(in14), .in1(in15), .out(multiplexer_2_out), .sel(ShiftAmt[0]));
  Multiplexer #(.enable("false")) multiplexer_3 (.in0(in13), .in1(in14), .out(multiplexer_3_out), .sel(ShiftAmt[0]));
  Multiplexer #(.enable("false")) multiplexer_4 (.in0(in12), .in1(in13), .out(multiplexer_4_out), .sel(ShiftAmt[0]));
  Multiplexer #(.enable("false")) multiplexer_5 (.in0(in11), .in1(in12), .out(multiplexer_5_out), .sel(ShiftAmt[0]));
  Multiplexer #(.enable("false")) multiplexer_6 (.in0(in10), .in1(in11), .out(multiplexer_6_out), .sel(ShiftAmt[0]));
  Multiplexer #(.enable("false")) multiplexer_7 (.in0(in9), .in1(in10), .out(multiplexer_7_out), .sel(ShiftAmt[0]));
  Multiplexer #(.enable("false")) multiplexer_8 (.in0(in8), .in1(in9), .out(multiplexer_8_out), .sel(ShiftAmt[0]));
  Multiplexer #(.enable("false")) multiplexer_9 (.in0(in7), .in1(in8), .out(multiplexer_9_out), .sel(ShiftAmt[0]));
  Multiplexer #(.enable("false")) multiplexer_10 (.in0(in6), .in1(in7), .out(multiplexer_10_out), .sel(ShiftAmt[0]));
  Multiplexer #(.enable("false")) multiplexer_11 (.in0(in5), .in1(in6), .out(multiplexer_11_out), .sel(ShiftAmt[0]));
  Multiplexer #(.enable("false")) multiplexer_12 (.in0(in4), .in1(in5), .out(multiplexer_12_out), .sel(ShiftAmt[0]));
  Multiplexer #(.enable("false")) multiplexer_13 (.in0(in3), .in1(in4), .out(multiplexer_13_out), .sel(ShiftAmt[0]));
  Multiplexer #(.enable("false")) multiplexer_14 (.in0(in2), .in1(in3), .out(multiplexer_14_out), .sel(ShiftAmt[0]));
  Multiplexer #(.enable("false")) multiplexer_15 (.in0(in1), .in1(in2), .out(multiplexer_15_out), .sel(ShiftAmt[0]));
  Multiplexer #(.enable("false")) multiplexer_16 (.in0(in0), .in1(in1), .out(multiplexer_16_out), .sel(ShiftAmt[0]));
  Multiplexer #(.enable("false")) multiplexer_17 (
    .in0(multiplexer_1_out), .in1(1'b0), .out(multiplexer_17_out), .sel(ShiftAmt[1]));
  Multiplexer #(.enable("false")) multiplexer_18 (
    .in0(multiplexer_2_out), .in1(1'b0), .out(multiplexer_18_out), .sel(ShiftAmt[1]));
  Multiplexer #(.enable("false")) multiplexer_19 (
    .in0(multiplexer_3_out), .in1(multiplexer_1_out), .out(multiplexer_19_out), .sel(ShiftAmt[1]));
  Multiplexer #(.enable("false")) multiplexer_20 (
    .in0(multiplexer_4_out), .in1(multiplexer_2_out), .out(multiplexer_20_out), .sel(ShiftAmt[1]));
  Multiplexer #(.enable("false")) multiplexer_21 (
    .in0(multiplexer_5_out), .in1(multiplexer_3_out), .out(multiplexer_21_out), .sel(ShiftAmt[1]));
  Multiplexer #(.enable("false")) multiplexer_22 (
    .in0(multiplexer_6_out), .in1(multiplexer_4_out), .out(multiplexer_22_out), .sel(ShiftAmt[1]));
  Multiplexer #(.enable("false")) multiplexer_23 (
    .in0(multiplexer_7_out), .in1(multiplexer_5_out), .out(multiplexer_23_out), .sel(ShiftAmt[1]));
  Multiplexer #(.enable("false")) multiplexer_24 (
    .in0(multiplexer_8_out), .in1(multiplexer_6_out), .out(multiplexer_24_out), .sel(ShiftAmt[1]));
  Multiplexer #(.enable("false")) multiplexer_25 (
    .in0(multiplexer_9_out), .in1(multiplexer_7_out), .out(multiplexer_25_out), .sel(ShiftAmt[1]));
  Multiplexer #(.enable("false")) multiplexer_26 (
    .in0(multiplexer_10_out), .in1(multiplexer_8_out), .out(multiplexer_26_out), .sel(ShiftAmt[1]));
  Multiplexer #(.enable("false")) multiplexer_27 (
    .in0(multiplexer_11_out), .in1(multiplexer_9_out), .out(multiplexer_27_out), .sel(ShiftAmt[1]));
  Multiplexer #(.enable("false")) multiplexer_28 (
    .in0(multiplexer_12_out), .in1(multiplexer_10_out), .out(multiplexer_28_out), .sel(ShiftAmt[1]));
  Multiplexer #(.enable("false")) multiplexer_29 (
    .in0(multiplexer_13_out), .in1(multiplexer_11_out), .out(multiplexer_29_out), .sel(ShiftAmt[1]));
  Multiplexer #(.enable("false")) multiplexer_30 (
    .in0(multiplexer_14_out), .in1(multiplexer_12_out), .out(multiplexer_30_out), .sel(ShiftAmt[1]));
  Multiplexer #(.enable("false")) multiplexer_31 (
    .in0(multiplexer_15_out), .in1(multiplexer_13_out), .out(multiplexer_31_out), .sel(ShiftAmt[1]));
  Multiplexer #(.enable("false")) multiplexer_32 (
    .in0(multiplexer_16_out), .in1(multiplexer_14_out), .out(multiplexer_32_out), .sel(ShiftAmt[1]));
  Multiplexer #(.enable("false")) multiplexer_33 (.in0(multiplexer_17_out), .in1(1'b0), .out(out15), .sel(ShiftAmt[2]));
  Multiplexer #(.enable("false")) multiplexer_34 (.in0(multiplexer_18_out), .in1(1'b0), .out(out14), .sel(ShiftAmt[2]));
  Multiplexer #(.enable("false")) multiplexer_35 (.in0(multiplexer_19_out), .in1(1'b0), .out(out13), .sel(ShiftAmt[2]));
  Multiplexer #(.enable("false")) multiplexer_36 (.in0(multiplexer_20_out), .in1(1'b0), .out(out12), .sel(ShiftAmt[2]));
  Multiplexer #(.enable("false")) multiplexer_37 (
    .in0(multiplexer_21_out), .in1(multiplexer_17_out), .out(out11), .sel(ShiftAmt[2]));
  Multiplexer #(.enable("false")) multiplexer_38 (
    .in0(multiplexer_22_out), .in1(multiplexer_18_out), .out(out10), .sel(ShiftAmt[2]));
  Multiplexer #(.enable("false")) multiplexer_39 (
    .in0(multiplexer_23_out), .in1(multiplexer_19_out), .out(out9), .sel(ShiftAmt[2]));
  Multiplexer #(.enable("false")) multiplexer_40 (
    .in0(multiplexer_24_out), .in1(multiplexer_20_out), .out(out8), .sel(ShiftAmt[2]));
  Multiplexer #(.enable("false")) multiplexer_41 (
    .in0(multiplexer_25_out), .in1(multiplexer_21_out), .out(out7), .sel(ShiftAmt[2]));
  Multiplexer #(.enable("false")) multiplexer_42 (
    .in0(multiplexer_26_out), .in1(multiplexer_22_out), .out(out6), .sel(ShiftAmt[2]));
  Multiplexer #(.enable("false")) multiplexer_43 (
    .in0(multiplexer_27_out), .in1(multiplexer_23_out), .out(out5), .sel(ShiftAmt[2]));
  Multiplexer #(.enable("false")) multiplexer_44 (
    .in0(multiplexer_28_out), .in1(multiplexer_24_out), .out(out4), .sel(ShiftAmt[2]));
  Multiplexer #(.enable("false")) multiplexer_45 (
    .in0(multiplexer_29_out), .in1(multiplexer_25_out), .out(out3), .sel(ShiftAmt[2]));
  Multiplexer #(.enable("false")) multiplexer_46 (
    .in0(multiplexer_30_out), .in1(multiplexer_26_out), .out(out2), .sel(ShiftAmt[2]));
  Multiplexer #(.enable("false")) multiplexer_47 (
    .in0(multiplexer_31_out), .in1(multiplexer_27_out), .out(out1), .sel(ShiftAmt[2]));
  Multiplexer #(.enable("false")) multiplexer_48 (
    .in0(multiplexer_32_out), .in1(multiplexer_28_out), .out(out0), .sel(ShiftAmt[2]));

  // Other names for the same wires on the sheet: S0 = ShiftAmt[0]; S1 = ShiftAmt[1]; S2 = ShiftAmt[2]
endmodule

module RShift (
  input  [2:0] ShiftAmt,
  input  in15,
  input  in14,
  input  in13,
  input  in12,
  input  in11,
  input  in10,
  input  in9,
  input  in8,
  input  in7,
  input  in6,
  input  in5,
  input  in4,
  input  in3,
  input  in2,
  input  in1,
  input  in0,
  output out15,
  output out14,
  output out13,
  output out12,
  output out11,
  output out10,
  output out9,
  output out8,
  output out7,
  output out6,
  output out5,
  output out4,
  output out3,
  output out2,
  output out1,
  output out0
);

  wire multiplexer_1_out, multiplexer_2_out, multiplexer_3_out, multiplexer_4_out, multiplexer_5_out,
       multiplexer_6_out, multiplexer_7_out, multiplexer_8_out, multiplexer_9_out, multiplexer_10_out,
       multiplexer_11_out, multiplexer_12_out, multiplexer_13_out, multiplexer_14_out, multiplexer_15_out,
       multiplexer_16_out, multiplexer_17_out, multiplexer_18_out, multiplexer_19_out, multiplexer_20_out,
       multiplexer_21_out, multiplexer_22_out, multiplexer_23_out, multiplexer_24_out, multiplexer_25_out,
       multiplexer_26_out, multiplexer_27_out, multiplexer_28_out, multiplexer_29_out, multiplexer_30_out,
       multiplexer_31_out, multiplexer_32_out;

  Multiplexer #(.enable("false")) multiplexer_1 (.in0(in15), .in1(in14), .out(multiplexer_1_out), .sel(ShiftAmt[0]));
  Multiplexer #(.enable("false")) multiplexer_2 (.in0(in14), .in1(in13), .out(multiplexer_2_out), .sel(ShiftAmt[0]));
  Multiplexer #(.enable("false")) multiplexer_3 (.in0(in13), .in1(in12), .out(multiplexer_3_out), .sel(ShiftAmt[0]));
  Multiplexer #(.enable("false")) multiplexer_4 (.in0(in12), .in1(in11), .out(multiplexer_4_out), .sel(ShiftAmt[0]));
  Multiplexer #(.enable("false")) multiplexer_5 (.in0(in11), .in1(in10), .out(multiplexer_5_out), .sel(ShiftAmt[0]));
  Multiplexer #(.enable("false")) multiplexer_6 (.in0(in10), .in1(in9), .out(multiplexer_6_out), .sel(ShiftAmt[0]));
  Multiplexer #(.enable("false")) multiplexer_7 (.in0(in9), .in1(in8), .out(multiplexer_7_out), .sel(ShiftAmt[0]));
  Multiplexer #(.enable("false")) multiplexer_8 (.in0(in8), .in1(in7), .out(multiplexer_8_out), .sel(ShiftAmt[0]));
  Multiplexer #(.enable("false")) multiplexer_9 (.in0(in7), .in1(in6), .out(multiplexer_9_out), .sel(ShiftAmt[0]));
  Multiplexer #(.enable("false")) multiplexer_10 (.in0(in6), .in1(in5), .out(multiplexer_10_out), .sel(ShiftAmt[0]));
  Multiplexer #(.enable("false")) multiplexer_11 (.in0(in5), .in1(in4), .out(multiplexer_11_out), .sel(ShiftAmt[0]));
  Multiplexer #(.enable("false")) multiplexer_12 (.in0(in4), .in1(in3), .out(multiplexer_12_out), .sel(ShiftAmt[0]));
  Multiplexer #(.enable("false")) multiplexer_13 (.in0(in3), .in1(in2), .out(multiplexer_13_out), .sel(ShiftAmt[0]));
  Multiplexer #(.enable("false")) multiplexer_14 (.in0(in2), .in1(in1), .out(multiplexer_14_out), .sel(ShiftAmt[0]));
  Multiplexer #(.enable("false")) multiplexer_15 (.in0(in1), .in1(in0), .out(multiplexer_15_out), .sel(ShiftAmt[0]));
  Multiplexer #(.enable("false")) multiplexer_16 (.in0(in0), .in1(1'b0), .out(multiplexer_16_out), .sel(ShiftAmt[0]));
  Multiplexer #(.enable("false")) multiplexer_17 (
    .in0(multiplexer_1_out), .in1(multiplexer_3_out), .out(multiplexer_17_out), .sel(ShiftAmt[1]));
  Multiplexer #(.enable("false")) multiplexer_18 (
    .in0(multiplexer_2_out), .in1(multiplexer_4_out), .out(multiplexer_18_out), .sel(ShiftAmt[1]));
  Multiplexer #(.enable("false")) multiplexer_19 (
    .in0(multiplexer_3_out), .in1(multiplexer_5_out), .out(multiplexer_19_out), .sel(ShiftAmt[1]));
  Multiplexer #(.enable("false")) multiplexer_20 (
    .in0(multiplexer_4_out), .in1(multiplexer_6_out), .out(multiplexer_20_out), .sel(ShiftAmt[1]));
  Multiplexer #(.enable("false")) multiplexer_21 (
    .in0(multiplexer_5_out), .in1(multiplexer_7_out), .out(multiplexer_21_out), .sel(ShiftAmt[1]));
  Multiplexer #(.enable("false")) multiplexer_22 (
    .in0(multiplexer_6_out), .in1(multiplexer_8_out), .out(multiplexer_22_out), .sel(ShiftAmt[1]));
  Multiplexer #(.enable("false")) multiplexer_23 (
    .in0(multiplexer_7_out), .in1(multiplexer_9_out), .out(multiplexer_23_out), .sel(ShiftAmt[1]));
  Multiplexer #(.enable("false")) multiplexer_24 (
    .in0(multiplexer_8_out), .in1(multiplexer_10_out), .out(multiplexer_24_out), .sel(ShiftAmt[1]));
  Multiplexer #(.enable("false")) multiplexer_25 (
    .in0(multiplexer_9_out), .in1(multiplexer_11_out), .out(multiplexer_25_out), .sel(ShiftAmt[1]));
  Multiplexer #(.enable("false")) multiplexer_26 (
    .in0(multiplexer_10_out), .in1(multiplexer_12_out), .out(multiplexer_26_out), .sel(ShiftAmt[1]));
  Multiplexer #(.enable("false")) multiplexer_27 (
    .in0(multiplexer_11_out), .in1(multiplexer_13_out), .out(multiplexer_27_out), .sel(ShiftAmt[1]));
  Multiplexer #(.enable("false")) multiplexer_28 (
    .in0(multiplexer_12_out), .in1(multiplexer_14_out), .out(multiplexer_28_out), .sel(ShiftAmt[1]));
  Multiplexer #(.enable("false")) multiplexer_29 (
    .in0(multiplexer_13_out), .in1(multiplexer_15_out), .out(multiplexer_29_out), .sel(ShiftAmt[1]));
  Multiplexer #(.enable("false")) multiplexer_30 (
    .in0(multiplexer_14_out), .in1(multiplexer_16_out), .out(multiplexer_30_out), .sel(ShiftAmt[1]));
  Multiplexer #(.enable("false")) multiplexer_31 (
    .in0(multiplexer_15_out), .in1(1'b0), .out(multiplexer_31_out), .sel(ShiftAmt[1]));
  Multiplexer #(.enable("false")) multiplexer_32 (
    .in0(multiplexer_16_out), .in1(1'b0), .out(multiplexer_32_out), .sel(ShiftAmt[1]));
  Multiplexer #(.enable("false")) multiplexer_33 (
    .in0(multiplexer_17_out), .in1(multiplexer_21_out), .out(out15), .sel(ShiftAmt[2]));
  Multiplexer #(.enable("false")) multiplexer_34 (
    .in0(multiplexer_18_out), .in1(multiplexer_22_out), .out(out14), .sel(ShiftAmt[2]));
  Multiplexer #(.enable("false")) multiplexer_35 (
    .in0(multiplexer_19_out), .in1(multiplexer_23_out), .out(out13), .sel(ShiftAmt[2]));
  Multiplexer #(.enable("false")) multiplexer_36 (
    .in0(multiplexer_20_out), .in1(multiplexer_24_out), .out(out12), .sel(ShiftAmt[2]));
  Multiplexer #(.enable("false")) multiplexer_37 (
    .in0(multiplexer_21_out), .in1(multiplexer_25_out), .out(out11), .sel(ShiftAmt[2]));
  Multiplexer #(.enable("false")) multiplexer_38 (
    .in0(multiplexer_22_out), .in1(multiplexer_26_out), .out(out10), .sel(ShiftAmt[2]));
  Multiplexer #(.enable("false")) multiplexer_39 (
    .in0(multiplexer_23_out), .in1(multiplexer_27_out), .out(out9), .sel(ShiftAmt[2]));
  Multiplexer #(.enable("false")) multiplexer_40 (
    .in0(multiplexer_24_out), .in1(multiplexer_28_out), .out(out8), .sel(ShiftAmt[2]));
  Multiplexer #(.enable("false")) multiplexer_41 (
    .in0(multiplexer_25_out), .in1(multiplexer_29_out), .out(out7), .sel(ShiftAmt[2]));
  Multiplexer #(.enable("false")) multiplexer_42 (
    .in0(multiplexer_26_out), .in1(multiplexer_30_out), .out(out6), .sel(ShiftAmt[2]));
  Multiplexer #(.enable("false")) multiplexer_43 (
    .in0(multiplexer_27_out), .in1(multiplexer_31_out), .out(out5), .sel(ShiftAmt[2]));
  Multiplexer #(.enable("false")) multiplexer_44 (
    .in0(multiplexer_28_out), .in1(multiplexer_32_out), .out(out4), .sel(ShiftAmt[2]));
  Multiplexer #(.enable("false")) multiplexer_45 (.in0(multiplexer_29_out), .in1(1'b0), .out(out3), .sel(ShiftAmt[2]));
  Multiplexer #(.enable("false")) multiplexer_46 (.in0(multiplexer_30_out), .in1(1'b0), .out(out2), .sel(ShiftAmt[2]));
  Multiplexer #(.enable("false")) multiplexer_47 (.in0(multiplexer_31_out), .in1(1'b0), .out(out1), .sel(ShiftAmt[2]));
  Multiplexer #(.enable("false")) multiplexer_48 (.in0(multiplexer_32_out), .in1(1'b0), .out(out0), .sel(ShiftAmt[2]));

  // Other names for the same wires on the sheet: S0 = ShiftAmt[0]; S1 = ShiftAmt[1]; S2 = ShiftAmt[2]
endmodule

module CheckSign6bit (
  input  [5:0] Input,
  output Sign___0____1
);


  assign Sign___0____1 = Input[5];
endmodule

module SignExtendNeg (
  input  [5:0] Input,
  output [15:0] Output
);

  wire [5:0] not_1_out;
  wire [15:0] alu_1_output;

  not not_1 (not_1_out[0], Input[0]);
  not not_2 (not_1_out[1], Input[1]);
  not not_3 (not_1_out[2], Input[2]);
  not not_4 (not_1_out[3], Input[3]);
  not not_5 (not_1_out[4], Input[4]);
  not not_6 (not_1_out[5], Input[5]);
  ALU alu_1 (
    .ALUOp(3'b000), .Input1({{10{1'b0}}, not_1_out}), .Input2(16'h1), .Output(alu_1_output));  // open: ShiftAmt, blt__bne
  Multiplexer #(.width(16), .enable("false")) multiplexer_1 (
    .in0({{10{1'b0}}, Input}), .in1(alu_1_output), .out(Output), .sel(Input[5]));
endmodule

// 6to16
module SignExtender6to16 (
  input  [5:0] Input,
  output [15:0] Output
);


  assign Output = {{10{1'b0}}, Input};
endmodule

// 12to16
module SignExtender12to16 (
  input  [11:0] Input,
  output [15:0] Output
);


  assign Output = {4'b0000, Input};
endmodule

module PC (
  input  Clock,
  input  Reset,
  input  [15:0] Input,
  input  Enable,
  output [15:0] out_5
);

  D_Flip_Flop d_ff_1 (.clk(Clock), .D(Input[0]), .Q(out_5[0]), .en(Enable), .reset(Reset));  // open: Qn, preset
  D_Flip_Flop d_ff_2 (.clk(Clock), .D(Input[2]), .Q(out_5[2]), .en(Enable), .reset(Reset));  // open: Qn, preset
  D_Flip_Flop d_ff_3 (.clk(Clock), .D(Input[4]), .Q(out_5[4]), .en(Enable), .reset(Reset));  // open: Qn, preset
  D_Flip_Flop d_ff_4 (.clk(Clock), .D(Input[6]), .Q(out_5[6]), .en(Enable), .reset(Reset));  // open: Qn, preset
  D_Flip_Flop d_ff_5 (.clk(Clock), .D(Input[8]), .Q(out_5[8]), .en(Enable), .reset(Reset));  // open: Qn, preset
  D_Flip_Flop d_ff_6 (.clk(Clock), .D(Input[10]), .Q(out_5[10]), .en(Enable), .reset(Reset));  // open: Qn, preset
  D_Flip_Flop d_ff_7 (.clk(Clock), .D(Input[12]), .Q(out_5[12]), .en(Enable), .reset(Reset));  // open: Qn, preset
  D_Flip_Flop d_ff_8 (.clk(Clock), .D(Input[14]), .Q(out_5[14]), .en(Enable), .reset(Reset));  // open: Qn, preset
  D_Flip_Flop d_ff_9 (.clk(Clock), .D(Input[1]), .Q(out_5[1]), .en(Enable), .reset(Reset));  // open: Qn, preset
  D_Flip_Flop d_ff_10 (.clk(Clock), .D(Input[3]), .Q(out_5[3]), .en(Enable), .reset(Reset));  // open: Qn, preset
  D_Flip_Flop d_ff_11 (.clk(Clock), .D(Input[5]), .Q(out_5[5]), .en(Enable), .reset(Reset));  // open: Qn, preset
  D_Flip_Flop d_ff_12 (.clk(Clock), .D(Input[7]), .Q(out_5[7]), .en(Enable), .reset(Reset));  // open: Qn, preset
  D_Flip_Flop d_ff_13 (.clk(Clock), .D(Input[9]), .Q(out_5[9]), .en(Enable), .reset(Reset));  // open: Qn, preset
  D_Flip_Flop d_ff_14 (.clk(Clock), .D(Input[11]), .Q(out_5[11]), .en(Enable), .reset(Reset));  // open: Qn, preset
  D_Flip_Flop d_ff_15 (.clk(Clock), .D(Input[13]), .Q(out_5[13]), .en(Enable), .reset(Reset));  // open: Qn, preset
  D_Flip_Flop d_ff_16 (.clk(Clock), .D(Input[15]), .Q(out_5[15]), .en(Enable), .reset(Reset));  // open: Qn, preset

  // Other names for the same wires on the sheet: E = Enable; in1 = Input[0]; InReg0[15:0] = Input; in2 = Input[1];
  //   in3 = Input[2]; in4 = Input[3]; in5 = Input[4]; in6 = Input[5]; in7 = Input[6]; in8 = Input[7]; in9 = Input[8];
  //   in10 = Input[9]; in11 = Input[10]; in12 = Input[11]; in13 = Input[12]; in14 = Input[13]; in15 = Input[14];
  //   in16 = Input[15]; out1 = out_5[0]; OutReg0[15:0] = out_5; out2 = out_5[1]; out3 = out_5[2]; out4 = out_5[3];
  //   out5 = out_5[4]; out6 = out_5[5]; out7 = out_5[6]; out8 = out_5[7]; out9 = out_5[8]; out10 = out_5[9];
  //   out11 = out_5[10]; out12 = out_5[11]; out13 = out_5[12]; out14 = out_5[13]; out15 = out_5[14];
  //   out16 = out_5[15]; R = Reset

  // Notes on the sheet:
  //   PC Register
endmodule

module _1_Bit_Adder (
  input  Carry_in,
  input  A,
  input  B,
  output Sum,
  output Carry_Out
);

  wire and_1_out, and_2_out, xor_1_out;

  and and_1 (and_1_out, B, A);
  or or_1 (Carry_Out, and_1_out, and_2_out);
  xor xor_1 (xor_1_out, A, B);
  and and_2 (and_2_out, xor_1_out, Carry_in);
  xor xor_2 (Sum, Carry_in, xor_1_out);
endmodule
